// Logisim project alu.circ as structural Verilog: 7 circuits, main circuit alu
module alu (
  input  [31:0] A,
  input  [31:0] B,
  input  [3:0] ALUSel,
  output [31:0] Result
);

  wire [31:0] add0, and1, not4, or2, sll6, slt7, sra5, sub8, xor3;

  add32 add32_1 (.in_1(A), .in_2(B), .Cin(1'b0), .out_4(add0));  // open: Cout
  assign and1 = A & B;  // AND_Gate and_1, 32 bits wide
  assign or2 = A | B;  // OR_Gate or_1, 32 bits wide
  assign xor3 = A ^ B;  // XOR_Gate xor_1, 32 bits wide
  assign not4 = ~A;  // NOT_Gate not_1, 32 bits wide
  Shifter #(.width(32), .shift("lr")) shifter_1 (.in(A), .\dist (B[4:0]), .out(sra5));
  Shifter #(.width(32)) shifter_2 (.in(A), .\dist (B[4:0]), .out(sll6));
  Subtractor #(.width(32)) subtractor_1 (.a(A), .b(B), .out(sub8));  // open: bin, bout
  assign slt7 = {{31{1'b0}}, sub8[31]};  // Bit_Extender bit_extender_1
  Multiplexer #(.select(4), .width(32), .enable("false")) multiplexer_1 (
    .in0(add0), .in1(and1), .in2(or2), .in3(xor3), .in4(not4), .in5(sra5), .in6(sll6), .in7(slt7),
    .in8(sub8), .out(Result), .sel(ALUSel));  // open: in9, in10, in11, in12, in13, in14, in15

  // Notes on the sheet:
  //   INPUTS to your circuit
  //   DON'T CHANGE THE LOCATIONS OF THE INPUTS AND OUTPUTS!
  //   OUTPUT from your circuit
endmodule

module add1 (
  input  A0,
  input  B0,
  input  Cin,
  output SUM,
  output Cout
);

  wire and_1_out, and_2_out, xor_1_out;

  xor xor_1 (xor_1_out, A0, B0);
  xor xor_2 (SUM, xor_1_out, Cin);
  and and_1 (and_1_out, Cin, xor_1_out);
  and and_2 (and_2_out, A0, B0);
  or or_1 (Cout, and_1_out, and_2_out);
endmodule

module add2 (
  input  [1:0] in_1,
  input  [1:0] in_2,
  input  Cin,
  output [1:0] SUM,
  output Cout
);

  wire add1_1_cout;

  add1 add1_1 (.A0(in_1[0]), .B0(in_2[0]), .Cin(Cin), .SUM(SUM[0]), .Cout(add1_1_cout));
  add1 add1_2 (.A0(in_1[1]), .B0(in_2[1]), .Cin(add1_1_cout), .SUM(SUM[1]), .Cout(Cout));

  // Other names for the same wires on the sheet: A[1:0] = in_1; A0 = in_1[0]; A1 = in_1[1]; B[1:0] = in_2;
  //   B0 = in_2[0]; B1 = in_2[1]; s1 = SUM[0]; s2 = SUM[1]
endmodule

module add4 (
  input  [3:0] in_1,
  input  [3:0] in_2,
  input  Cin,
  output [3:0] SUM,
  output Cout
);

  wire add2_1_cout;

  add2 add2_1 (.in_1(in_1[1:0]), .in_2(in_2[1:0]), .Cin(Cin), .SUM(SUM[1:0]), .Cout(add2_1_cout));
  add2 add2_2 (.in_1(in_1[3:2]), .in_2(in_2[3:2]), .Cin(add2_1_cout), .SUM(SUM[3:2]), .Cout(Cout));

  // Other names for the same wires on the sheet: A[3:0] = in_1; A0[1:0] = in_1[1:0]; A1[1:0] = in_1[3:2];
  //   B[3:0] = in_2; B0[1:0] = in_2[1:0]; B1[1:0] = in_2[3:2]; s1[1:0] = SUM[1:0]; s2[1:0] = SUM[3:2]
endmodule

module add8 (
  input  [7:0] in_1,
  input  [7:0] in_2,
  input  Cin,
  output [7:0] SUM,
  output Cout
);

  wire add4_1_cout;

  add4 add4_1 (.in_1(in_1[3:0]), .in_2(in_2[3:0]), .Cin(Cin), .SUM(SUM[3:0]), .Cout(add4_1_cout));
  add4 add4_2 (.in_1(in_1[7:4]), .in_2(in_2[7:4]), .Cin(add4_1_cout), .SUM(SUM[7:4]), .Cout(Cout));

  // Other names for the same wires on the sheet: A[7:0] = in_1; A0[3:0] = in_1[3:0]; A1[3:0] = in_1[7:4];
  //   B[7:0] = in_2; B0[3:0] = in_2[3:0]; B1[3:0] = in_2[7:4]; s1[3:0] = SUM[3:0]; s2[3:0] = SUM[7:4]
endmodule

module add16 (
  input  [15:0] in_1,
  input  [15:0] in_2,
  input  Cin,
  output [15:0] SUM,
  output Cout
);

  wire add8_1_cout;

  add8 add8_1 (.in_1(in_1[7:0]), .in_2(in_2[7:0]), .Cin(Cin), .SUM(SUM[7:0]), .Cout(add8_1_cout));
  add8 add8_2 (.in_1(in_1[15:8]), .in_2(in_2[15:8]), .Cin(add8_1_cout), .SUM(SUM[15:8]), .Cout(Cout));

  // Other names for the same wires on the sheet: A[15:0] = in_1; A0[7:0] = in_1[7:0]; A1[7:0] = in_1[15:8];
  //   B[15:0] = in_2; B0[7:0] = in_2[7:0]; B1[7:0] = in_2[15:8]; s1[7:0] = SUM[7:0]; s2[7:0] = SUM[15:8]
endmodule

module add32 (
  input  [31:0] in_1,
  input  [31:0] in_2,
  input  Cin,
  output [31:0] out_4,
  output Cout
);

  wire add16_1_cout;

  add16 add16_1 (.in_1(in_1[15:0]), .in_2(in_2[15:0]), .Cin(Cin), .SUM(out_4[15:0]), .Cout(add16_1_cout));
  add16 add16_2 (.in_1(in_1[31:16]), .in_2(in_2[31:16]), .Cin(add16_1_cout), .SUM(out_4[31:16]), .Cout(Cout));

  // Other names for the same wires on the sheet: A[31:0] = in_1; A0[15:0] = in_1[15:0]; A1[15:0] = in_1[31:16];
  //   B[31:0] = in_2; B0[15:0] = in_2[15:0]; B1[15:0] = in_2[31:16]; s1[15:0] = out_4[15:0]; SUM[31:0] = out_4;
  //   s2[15:0] = out_4[31:16]

  // Notes on the sheet:
  //   SUM
endmodule
