// Logisim project regfile.circ as structural Verilog: 2 circuits, main circuit main
module main (
  input  [4:0] rs1,
  input  [4:0] rs2,
  input  [4:0] rd,
  input  [31:0] Write_Data,
  input  RegWEn,
  input  clk,
  output [31:0] ra,
  output [31:0] sp,
  output [31:0] t0,
  output [31:0] t1,
  output [31:0] t2,
  output [31:0] s0,
  output [31:0] s1,
  output [31:0] a0,
  output [31:0] Read_Data_1,
  output [31:0] Read_Data_2
);


  // Other names for the same wires on the sheet: read_data1[31:0] = Read_Data_1; read_data2[31:0] = Read_Data_2;
  //   read_reg1[4:0] = rs1; read_reg2[4:0] = rs2; write_en = RegWEn; write_reg[4:0] = rd

  // Notes on the sheet:
  //   INPUTS to your circuit
  //   DON'T CHANGE THE LOCATIONS OF THE INPUTS AND OUTPUTS!
  //   These are DEBUG/TEST outputs from your circuit.
  //   OUTPUTS from your circuit
endmodule

module regfilesadness (
  input  reset,
  input  clk,
  input  WE,
  input  [31:0] in_4,
  output [31:0] out_5
);

  wire in_put;

  and and_1 (in_put, clk, WE);
  D_Flip_Flop d_ff_1 (.D(in_4[0]), .clk(in_put), .Q(out_5[0]), .reset(reset));  // open: Qn, preset
  D_Flip_Flop d_ff_2 (.D(in_4[1]), .clk(in_put), .Q(out_5[1]), .reset(reset));  // open: Qn, preset
  D_Flip_Flop d_ff_3 (.D(in_4[2]), .clk(in_put), .Q(out_5[2]), .reset(reset));  // open: Qn, preset
  D_Flip_Flop d_ff_4 (.D(in_4[3]), .clk(in_put), .Q(out_5[3]), .reset(reset));  // open: Qn, preset
  D_Flip_Flop d_ff_5 (.D(in_4[4]), .clk(in_put), .Q(out_5[4]), .reset(reset));  // open: Qn, preset
  D_Flip_Flop d_ff_6 (.D(in_4[5]), .clk(in_put), .Q(out_5[5]), .reset(reset));  // open: Qn, preset
  D_Flip_Flop d_ff_7 (.D(in_4[6]), .clk(in_put), .Q(out_5[6]), .reset(reset));  // open: Qn, preset
  D_Flip_Flop d_ff_8 (.D(in_4[7]), .clk(in_put), .Q(out_5[7]), .reset(reset));  // open: Qn, preset
  D_Flip_Flop d_ff_9 (.D(in_4[9]), .clk(in_put), .Q(out_5[9]), .reset(reset));  // open: Qn, preset
  D_Flip_Flop d_ff_10 (.D(in_4[8]), .clk(in_put), .Q(out_5[8]), .reset(reset));  // open: Qn, preset
  D_Flip_Flop d_ff_11 (.D(in_4[10]), .clk(in_put), .Q(out_5[10]), .reset(reset));  // open: Qn, preset
  D_Flip_Flop d_ff_12 (.D(in_4[11]), .clk(in_put), .Q(out_5[11]), .reset(reset));  // open: Qn, preset
  D_Flip_Flop d_ff_13 (.D(in_4[12]), .clk(in_put), .Q(out_5[12]), .reset(reset));  // open: Qn, preset
  D_Flip_Flop d_ff_14 (.D(in_4[13]), .clk(in_put), .Q(out_5[13]), .reset(reset));  // open: Qn, preset
  D_Flip_Flop d_ff_15 (.D(in_4[14]), .clk(in_put), .Q(out_5[14]), .reset(reset));  // open: Qn, preset
  D_Flip_Flop d_ff_16 (.D(in_4[15]), .clk(in_put), .Q(out_5[15]), .reset(reset));  // open: Qn, preset
  D_Flip_Flop d_ff_17 (.D(in_4[16]), .clk(in_put), .Q(out_5[16]), .reset(reset));  // open: Qn, preset
  D_Flip_Flop d_ff_18 (.D(in_4[17]), .clk(in_put), .Q(out_5[17]), .reset(reset));  // open: Qn, preset
  D_Flip_Flop d_ff_19 (.D(in_4[18]), .clk(in_put), .Q(out_5[18]), .reset(reset));  // open: Qn, preset
  D_Flip_Flop d_ff_20 (.D(in_4[19]), .clk(in_put), .Q(out_5[19]), .reset(reset));  // open: Qn, preset
  D_Flip_Flop d_ff_21 (.D(in_4[20]), .clk(in_put), .Q(out_5[20]), .reset(reset));  // open: Qn, preset
  D_Flip_Flop d_ff_22 (.D(in_4[21]), .clk(in_put), .Q(out_5[21]), .reset(reset));  // open: Qn, preset
  D_Flip_Flop d_ff_23 (.D(in_4[22]), .clk(in_put), .Q(out_5[22]), .reset(reset));  // open: Qn, preset
  D_Flip_Flop d_ff_24 (.D(in_4[23]), .clk(in_put), .Q(out_5[23]), .reset(reset));  // open: Qn, preset
  D_Flip_Flop d_ff_25 (.D(in_4[25]), .clk(in_put), .Q(out_5[25]), .reset(reset));  // open: Qn, preset
  D_Flip_Flop d_ff_26 (.D(in_4[24]), .clk(in_put), .Q(out_5[24]), .reset(reset));  // open: Qn, preset
  D_Flip_Flop d_ff_27 (.D(in_4[26]), .clk(in_put), .Q(out_5[26]), .reset(reset));  // open: Qn, preset
  D_Flip_Flop d_ff_28 (.D(in_4[27]), .clk(in_put), .Q(out_5[27]), .reset(reset));  // open: Qn, preset
  D_Flip_Flop d_ff_29 (.D(in_4[28]), .clk(in_put), .Q(out_5[28]), .reset(reset));  // open: Qn, preset
  D_Flip_Flop d_ff_30 (.D(in_4[29]), .clk(in_put), .Q(out_5[29]), .reset(reset));  // open: Qn, preset
  D_Flip_Flop d_ff_31 (.D(in_4[30]), .clk(in_put), .Q(out_5[30]), .reset(reset));  // open: Qn, preset
  D_Flip_Flop d_ff_32 (.D(in_4[31]), .clk(in_put), .Q(out_5[31]), .reset(reset));  // open: Qn, preset

  // Other names for the same wires on the sheet: in0 = in_4[0]; in1 = in_4[1]; in2 = in_4[2]; in3 = in_4[3];
  //   in4 = in_4[4]; in5 = in_4[5]; in6 = in_4[6]; in7 = in_4[7]; in8 = in_4[8]; in9 = in_4[9]; in10 = in_4[10];
  //   in11 = in_4[11]; in12 = in_4[12]; in13 = in_4[13]; in14 = in_4[14]; in15 = in_4[15]; in16 = in_4[16];
  //   in17 = in_4[17]; in18 = in_4[18]; in19 = in_4[19]; in20 = in_4[20]; in21 = in_4[21]; in22 = in_4[22];
  //   in23 = in_4[23]; in24 = in_4[24]; in25 = in_4[25]; in26 = in_4[26]; in27 = in_4[27]; in28 = in_4[28];
  //   in29 = in_4[29]; in30 = in_4[30]; in31 = in_4[31]; out0 = out_5[0]; out1 = out_5[1]; out2 = out_5[2];
  //   out3 = out_5[3]; out4 = out_5[4]; out5 = out_5[5]; out6 = out_5[6]; out7 = out_5[7]; out8 = out_5[8];
  //   out9 = out_5[9]; out10 = out_5[10]; out11 = out_5[11]; out12 = out_5[12]; out13 = out_5[13]; out14 = out_5[14];
  //   out15 = out_5[15]; out16 = out_5[16]; out17 = out_5[17]; out18 = out_5[18]; out19 = out_5[19];
  //   out20 = out_5[20]; out21 = out_5[21]; out22 = out_5[22]; out23 = out_5[23]; out24 = out_5[24];
  //   out25 = out_5[25]; out26 = out_5[26]; out27 = out_5[27]; out28 = out_5[28]; out29 = out_5[29];
  //   out30 = out_5[30]; out31 = out_5[31]

  // Notes on the sheet:
  //   data
endmodule
